// Logisim project MIPS.circ as structural Verilog: 12 circuits, main circuit main
module main (
  output [3:0] t0,
  output [3:0] t1,
  output [3:0] t2,
  output [3:0] t3,
  output [3:0] t4,
  output [3:0] sp
);

  wire alu_4bit_1_zero, clock_1_out, control_unit_1_alu_src, control_unit_1_beq, control_unit_1_bneq,
       control_unit_1_jump, control_unit_1_memread, control_unit_1_memtoreg, control_unit_1_memwrite,
       control_unit_1_regdst, control_unit_1_regwrite, n7408_1_p3, n7408_1_p5, n7408_1_p6, n7408_1_p8,
       n7408_1_p9, n7408_1_p10;
  wire [2:0] control_unit_1_alu_op;
  wire [3:0] alu_4bit_1_out, Data_Memory_read_data, data_registers_1_read_data_1,
       data_registers_1_read_data_2, Instruction_Memory_dst_reg_shamt_addr__immdt__0_3,
       Instruction_Memory_opcode__12_15, Instruction_Memory_src_reg_1__8_11,
       Instruction_Memory_src_reg_2_dst_reg__4_7, Mux_2_dataout, mux_4bit_1_dataout, mux_4bit_2_dataout,
       Mux_dataout;
  wire [7:0] mux_8bit_1_out, n8bit_adder_1_out, PC_q;

  Clock clock_1 (.out(clock_1_out));
  Register_part PC (.D(mux_8bit_1_out), .en(1'b1), .Q(PC_q), .clk(clock_1_out));  // open: clr
  // Probe on PC_q
  Instruction Instruction_Memory (
    .PC(PC_q), .Opcode__12_15(Instruction_Memory_opcode__12_15),
    .Src_Reg_1__8_11(Instruction_Memory_src_reg_1__8_11),
    .Src_Reg_2_Dst_Reg__4_7(Instruction_Memory_src_reg_2_dst_reg__4_7),
    .Dst_Reg_Shamt_Addr__Immdt__0_3(Instruction_Memory_dst_reg_shamt_addr__immdt__0_3));
  _8Bit_Adder u_8bit_adder_1 (
    .A(PC_q), .B({4'b0000, mux_4bit_1_dataout}), .Cin(1'b1), .Out(n8bit_adder_1_out));  // open: Cout
  Control_unit control_unit_1 (
    .OP_CODE(Instruction_Memory_opcode__12_15), .RegWrite(control_unit_1_regwrite),
    .ALU_Src(control_unit_1_alu_src), .MemWrite(control_unit_1_memwrite), .ALU_op(control_unit_1_alu_op),
    .MemToReg(control_unit_1_memtoreg), .MemRead(control_unit_1_memread), .Bneq(control_unit_1_bneq),
    .Beq(control_unit_1_beq), .Jump(control_unit_1_jump), .RegDst(control_unit_1_regdst));
  MUX_4Bit Mux (
    .S(control_unit_1_regdst), .Data0(Instruction_Memory_src_reg_2_dst_reg__4_7),
    .Data1(Instruction_Memory_dst_reg_shamt_addr__immdt__0_3), .DataOut(Mux_dataout));
  Data_registers data_registers_1 (
    .Reg_1_Address(Instruction_Memory_src_reg_1__8_11),
    .Reg_2_Address(Instruction_Memory_src_reg_2_dst_reg__4_7), .Write_Reg_Address(Mux_dataout),
    .Write_Data(Mux_2_dataout), .Clk(clock_1_out), .RegWrite(control_unit_1_regwrite),
    .Read_Data_1(data_registers_1_read_data_1), .Read_Data_2(data_registers_1_read_data_2), .t0(t0), .t1(t1),
    .t2(t2), .t3(t3), .t4(t4), .sp(sp));  // open: zero
  MUX_4Bit mux_4bit_1 (
    .S(n7408_1_p10), .Data0(4'b0000), .Data1(Instruction_Memory_dst_reg_shamt_addr__immdt__0_3),
    .DataOut(mux_4bit_1_dataout));
  MUX_4Bit mux_4bit_2 (
    .S(control_unit_1_alu_src), .Data0(data_registers_1_read_data_2),
    .Data1(Instruction_Memory_dst_reg_shamt_addr__immdt__0_3), .DataOut(mux_4bit_2_dataout));
  ALU_4Bit alu_4bit_1 (
    .A(data_registers_1_read_data_1), .B(mux_4bit_2_dataout), .ALUop(control_unit_1_alu_op),
    .Out(alu_4bit_1_out), .Zero(alu_4bit_1_zero));  // open: Carry_Borrow
  // _7408 7408_1: pin names not known; wires that end beside it: control_unit_1_beq, alu_4bit_1_zero, n7408_1_p3, control_unit_1_bneq, n7408_1_p5, n7408_1_p6, 1'b1, n7408_1_p8, n7408_1_p9, n7408_1_p10
  // _7404 7404_1: pin names not known; wires that end beside it: 1'b0, alu_4bit_1_zero, n7408_1_p5, n7408_1_p3, n7408_1_p8, n7408_1_p6, n7408_1_p9, 1'b0, 1'b1
  Data_Memory Data_Memory (
    .Address(alu_4bit_1_out), .Write_Data(data_registers_1_read_data_2), .CLK(clock_1_out),
    .MemWrite(control_unit_1_memwrite), .MemRead(control_unit_1_memread), .Read_Data(Data_Memory_read_data));
  MUX_8Bit mux_8bit_1 (
    .S(control_unit_1_jump), .A(n8bit_adder_1_out),
    .B({Instruction_Memory_src_reg_1__8_11, Instruction_Memory_src_reg_2_dst_reg__4_7}), .Out(mux_8bit_1_out));
  // Probe on mux_8bit_1_out
  MUX_4Bit Mux_2 (
    .S(control_unit_1_memtoreg), .Data0(alu_4bit_1_out), .Data1(Data_Memory_read_data),
    .DataOut(Mux_2_dataout));
endmodule

// Control
module Control_unit (
  input  [3:0] OP_CODE,
  output RegWrite,
  output ALU_Src,
  output MemWrite,
  output [2:0] ALU_op,
  output MemToReg,
  output MemRead,
  output Bneq,
  output Beq,
  output Jump,
  output RegDst
);

  ROM #(.addrWidth(4), .dataWidth(12)) rom_1 (
    .addr(OP_CODE), .data({RegDst, Jump, Beq, Bneq, MemRead, MemToReg, ALU_op, MemWrite, ALU_Src, RegWrite}));  // open: sel
  // Probe on {RegDst, Jump, Beq, Bneq, MemRead, MemToReg, ALU_op, MemWrite, ALU_Src, RegWrite}

  // Notes on the sheet:
  //   contents of rom_1 (hex, n*v repeats v):
  //   801 13 6 108 811 3 1b 208 c3 831 b 400 819 809 821 829
endmodule

// ALU
module ALU_4Bit (
  input  [2:0] ALUop,
  input  [3:0] A,
  input  [3:0] B,
  output [3:0] Out,
  output Carry_Borrow,
  output Zero
);

  wire adder_1_cout, comparator_1_gt, subtractor_1_bout;
  wire [1:0] bit_extender_1_out;
  wire [3:0] adder_1_out, and_1_out, multiplexer_1_out, nor_1_out, or_1_out, shifter_1_out, shifter_2_out,
       subtractor_1_out;

  Subtractor #(.width(4)) subtractor_1 (.a(A), .b(B), .out(subtractor_1_out), .bout(subtractor_1_bout));  // open: bin
  assign and_1_out = A & B;  // AND_Gate and_1, 4 bits wide
  assign or_1_out = A | B;  // OR_Gate or_1, 4 bits wide
  assign nor_1_out = ~(A | B);  // NOR_Gate nor_1, 4 bits wide
  Comparator #(.width(4)) comparator_1 (.a(B), .b(4'b0011), .gt(comparator_1_gt));  // open: eq, lt
  Shifter #(.width(4)) shifter_1 (.in(B), .\dist (bit_extender_1_out), .out(shifter_1_out));
  Adder #(.width(4)) adder_1 (.a(A), .b(B), .out(adder_1_out), .cout(adder_1_cout));  // open: cin
  Shifter #(.width(4)) shifter_2 (.in(A), .\dist (bit_extender_1_out), .out(shifter_2_out));
  Multiplexer #(.width(4), .enable("false")) multiplexer_1 (
    .in0(B), .in1(4'b0011), .out(multiplexer_1_out), .sel(comparator_1_gt));
  Bit_Extender #(.in_width(4), .out_width(2)) bit_extender_1 (.in(multiplexer_1_out), .out(bit_extender_1_out));
  Multiplexer #(.select(3), .width(4), .enable("false")) multiplexer_2 (
    .in0(adder_1_out), .in1(subtractor_1_out), .in2(and_1_out), .in3(or_1_out), .in4(nor_1_out),
    .in5(shifter_2_out), .in6(shifter_1_out), .in7(4'b0000), .out(Out), .sel(ALUop));
  Multiplexer #(.select(3), .enable("false")) multiplexer_3 (
    .in0(adder_1_cout), .in1(subtractor_1_bout), .in2(1'b0), .in3(1'b0), .in4(1'b0), .in5(1'b0), .in6(1'b0),
    .in7(1'b0), .out(Carry_Borrow), .sel(ALUop));
  nor nor_2 (Zero, Out[0], Out[1], Out[2], Out[3]);

  // Notes on the sheet:
  //   000 Add
  //   001 Sub
  //   010 And
  //   011 Or
  //   100 Nor
  //   101 SL
  //   110 SR
  //   111 Zero
endmodule

// Mux
module MUX_4Bit (
  input  S,
  input  [3:0] Data0,
  input  [3:0] Data1,
  output [3:0] DataOut
);

  // _74157 74157_1: pin names not known; wires that end beside it: S, Data0[0], Data1[0], DataOut[0], Data0[1], Data1[1], DataOut[1], 1'b0, 1'b1, 1'b0, Data0[3], Data1[3], DataOut[3], Data0[2], Data1[2], DataOut[2]
endmodule

module Instruction (
  input  [7:0] PC,
  output [3:0] Opcode__12_15,
  output [3:0] Src_Reg_1__8_11,
  output [3:0] Src_Reg_2_Dst_Reg__4_7,
  output [3:0] Dst_Reg_Shamt_Addr__Immdt__0_3
);

  ROM #(.dataWidth(16)) rom_1 (
    .addr(PC), .data({Opcode__12_15, Src_Reg_1__8_11, Src_Reg_2_Dst_Reg__4_7, Dst_Reg_Shamt_Addr__Immdt__0_3}));  // open: sel

  // Notes on the sheet:
  //   contents of rom_1 (hex, n*v repeats v):
  //   301e 302d 3030 3040 3050 c02a 304f e414 3441 e344 2448 a041 3551 d313 4221 9050 d301 d502 9000
endmodule

// REG
module Register (
  input  [3:0] in_1,
  input  Clock,
  output [3:0] Out
);

  // _7474 7474_1: pin names not known; wires that end beside it: in_1[0], Clock, Out[0], 1'b0, 1'b1, in_1[1], Clock, Out[1]
  // _7474 7474_2: pin names not known; wires that end beside it: in_1[2], Clock, Out[2], 1'b0, 1'b1, in_1[3], Clock, Out[3]
endmodule

module All_Registers (
  input  Clock_zero,
  input  [3:0] t0_in,
  input  Clock0,
  input  [3:0] t1_in,
  input  Clock1,
  input  [3:0] t2_in,
  input  Clock2,
  input  [3:0] t3_in,
  input  Clock3,
  input  [3:0] t4_in,
  input  Clock4,
  input  [3:0] sp_in,
  input  Clock4_2,
  output [3:0] Zero,
  output [3:0] t0,
  output [3:0] t1,
  output [3:0] t2,
  output [3:0] t3,
  output [3:0] t4,
  output [3:0] sp_out
);

  Register register_1 (.in_1(t0_in), .Clock(Clock0), .Out(t0));
  Register register_2 (.in_1(t1_in), .Clock(Clock1), .Out(t1));
  Register register_3 (.in_1(t2_in), .Clock(Clock2), .Out(t2));
  Register register_4 (.in_1(t3_in), .Clock(Clock3), .Out(t3));
  Register register_5 (.in_1(t4_in), .Clock(Clock4), .Out(t4));
  Register register_6 (.in_1(sp_in), .Clock(Clock4_2), .Out(sp_out));

  assign Zero = 4'b0000;
endmodule

// Registers
module Data_registers (
  input  RegWrite,
  input  [3:0] Reg_1_Address,
  input  [3:0] Reg_2_Address,
  input  [3:0] Write_Reg_Address,
  input  [3:0] Write_Data,
  input  Clk,
  output [3:0] Read_Data_1,
  output [3:0] Read_Data_2,
  output [3:0] zero,
  output [3:0] t0,
  output [3:0] t1,
  output [3:0] t2,
  output [3:0] t3,
  output [3:0] t4,
  output [3:0] sp
);

  wire and_1_out, decoder_1_out0, decoder_1_out1, decoder_1_out2, decoder_1_out3, decoder_1_out4,
       decoder_1_out5, decoder_1_out6;
  wire [2:0] multiplexer_1_out;

  Multiplexer #(.width(3), .enable("false")) multiplexer_1 (
    .in0(3'b000), .in1(Write_Reg_Address[2:0]), .out(multiplexer_1_out), .sel(and_1_out));
  and and_1 (and_1_out, RegWrite, Clk);
  Decoder #(.select(3), .enable("false")) decoder_1 (
    .out0(decoder_1_out0), .out1(decoder_1_out1), .out2(decoder_1_out2), .out3(decoder_1_out3),
    .out4(decoder_1_out4), .out5(decoder_1_out5), .out6(decoder_1_out6), .sel(multiplexer_1_out));  // open: out7
  All_Registers all_registers_1 (
    .Clock_zero(decoder_1_out0), .t0_in(Write_Data), .Clock0(decoder_1_out1), .t1_in(Write_Data),
    .Clock1(decoder_1_out2), .t2_in(Write_Data), .Clock2(decoder_1_out3), .t3_in(Write_Data),
    .Clock3(decoder_1_out4), .t4_in(Write_Data), .Clock4(decoder_1_out5), .sp_in(Write_Data),
    .Clock4_2(decoder_1_out6), .Zero(zero), .t0(t0), .t1(t1), .t2(t2), .t3(t3), .t4(t4), .sp_out(sp));
  Multiplexer #(.select(3), .width(4), .enable("false")) multiplexer_2 (
    .in0(zero), .in1(t0), .in2(t1), .in3(t2), .in4(t3), .in5(t4), .in6(sp), .out(Read_Data_1),
    .sel(Reg_1_Address[2:0]));  // open: in7
  Multiplexer #(.select(3), .width(4), .enable("false")) multiplexer_3 (
    .in0(zero), .in1(t0), .in2(t1), .in3(t2), .in4(t3), .in5(t4), .in6(sp), .out(Read_Data_2),
    .sel(Reg_2_Address[2:0]));  // open: in7
endmodule

module Alu_Control (
  input  beq,
  input  bneq,
  input  [3:0] Read_Data_1,
  input  [3:0] Read_Data_2,
  input  [2:0] ALUop,
  output bsel,
  output [3:0] out
);

  wire alu_4bit_1_zero, n7408_1_p3, n7408_1_p6, not_1_out;

  ALU_4Bit alu_4bit_1 (
    .A(Read_Data_1), .B(Read_Data_2), .ALUop(ALUop), .Out(out), .Zero(alu_4bit_1_zero));  // open: Carry_Borrow
  not not_1 (not_1_out, alu_4bit_1_zero);
  or or_1 (bsel, n7408_1_p3, n7408_1_p6);
  // _7408 7408_1: pin names not known; wires that end beside it: beq, alu_4bit_1_zero, n7408_1_p3, bneq, not_1_out, n7408_1_p6
endmodule

module Data_Memory (
  input  MemWrite,
  input  MemRead,
  input  [3:0] Address,
  input  [3:0] Write_Data,
  input  CLK,
  output [3:0] Read_Data
);

  RAM #(.addrWidth(4), .dataWidth(4), .bus("separate")) ram_1 (
    .addr(Address), .din(Write_Data), .data(Read_Data), .str(MemWrite), .clk(CLK), .ld(MemRead));  // open: sel, clr
endmodule

module _8Bit_Adder (
  input  [7:0] A,
  input  [7:0] B,
  input  Cin,
  output Cout,
  output [7:0] Out
);

  wire n7483_ic_2__14__cout;

  _7483_IC u_7483_ic_1 (
    ._1__A4(B[7]), ._2__S3(Out[6]), ._3__A3(B[6]), ._4__B3(A[6]), ._5__Vcc(1'b1), ._6__S2(Out[5]),
    ._7__B2(A[5]), ._8__A2(B[5]), ._16__B4(A[7]), ._15__S4(Out[7]), ._14__Cout(Cout),
    ._13__Cin(n7483_ic_2__14__cout), ._12__GND(1'b0), ._11__B1(A[4]), ._10__A1(B[4]), ._9__S1(Out[4]));
  _7483_IC u_7483_ic_2 (
    ._1__A4(B[3]), ._2__S3(Out[2]), ._3__A3(B[2]), ._4__B3(A[2]), ._5__Vcc(1'b1), ._6__S2(Out[1]),
    ._7__B2(A[1]), ._8__A2(B[1]), ._16__B4(A[3]), ._15__S4(Out[3]), ._14__Cout(n7483_ic_2__14__cout),
    ._13__Cin(Cin), ._12__GND(1'b0), ._11__B1(A[0]), ._10__A1(B[0]), ._9__S1(Out[0]));
endmodule

module MUX_8Bit (
  input  S,
  input  [7:0] A,
  input  [7:0] B,
  output [7:0] Out
);

  MUX_4Bit mux_4bit_1 (.S(S), .Data0(A[3:0]), .Data1(B[3:0]), .DataOut(Out[3:0]));
  MUX_4Bit mux_4bit_2 (.S(S), .Data0(A[7:4]), .Data1(B[7:4]), .DataOut(Out[7:4]));
endmodule
